# Fritzing sketch esp-rfm-bridge (saved by Fritzing 0.9.3b)
perfboards: 1

parts:
  U1 = NodeMCU V3.0
  JP1 = Header 5x2 [package=2x5-shrouded_smd]

nets:
  N1: U1.D1, JP1.3
  N2: U1.3V3, JP1.8
  N3: U1.GND#6, U1.GND#13, U1.GND#16, U1.GND#33, JP1.5
  N4: U1.D5, JP1.2
  N5: U1.D6, JP1.4
  N6: U1.D7, JP1.6
  N7: U1.D8, JP1.1

custom parts:
  NodeMCU V3.0: ESP8266 based NodeMCU
